# Fritzing sketch circuit (saved by Fritzing 1.0.6)
breadboards: 1

parts:
  A1 = Raspberry Pi 5
  L298N2 = L298N DC motor driver
  Part2 = Arduino Nano (Rev3.0) (ICSP)
  DC_Mot_Enc2 = DC Motor with two-phase hall-encoder [part_number=VT-E-G25A-06-177E]
  Part3 = Adafruit BNO085 9-DOF Orientation IMU Fusion [part_number="Addfruit #4754"]
  U2 = LIPO-2000mAh [package=lipo-2000]
  J1 = Basic Servo
  HC-SR04_Sensor_1 = HC-SR04 Ultrasonic Distance Sensor
  HC-SR04_Sensor_2 = HC-SR04 Ultrasonic Distance Sensor
  HC-SR04_Sensor_3 = HC-SR04 Ultrasonic Distance Sensor
  HC-SR04_Sensor_4 = HC-SR04 Ultrasonic Distance Sensor

nets:
  GND: A1.GND, L298N2.GND, U2.-
  N1: A1.GPIO4, HC-SR04_Sensor_2.ECHO
  N2: A1.GPIO14, Part3.SCL/SCK/RX
  N3: A1.GPIO15, Part3.SDA/MISO/TX
  N4: A1.GPIO17, HC-SR04_Sensor_3.ECHO
  N5: A1.GPIO27, HC-SR04_Sensor_3.TRIG
  N6: A1.GPIO23, DC_Mot_Enc2.pin3
  N7: A1.GPIO24, DC_Mot_Enc2.pin4
  N8: A1.GPIO10, HC-SR04_Sensor_1.ECHO
  N9: A1.GPIO9, HC-SR04_Sensor_1.TRIG
  N10: A1.GPIO11, HC-SR04_Sensor_2.TRIG
  N11: A1.GPIO13, HC-SR04_Sensor_4.ECHO
  N12: A1.GPIO26, HC-SR04_Sensor_4.TRIG
  N13: L298N2.OUT1, DC_Mot_Enc2.pin6
  N14: L298N2.OUT2, DC_Mot_Enc2.pin1
  N15: L298N2.12V, U2.+
  5V: L298N2.5V, J1.vcc
  N16: L298N2.IN1, Part2.D11/MOSI
  N17: L298N2.IN2, Part2.D10
  N18: Part2.D9, J1.pulse
  GND_2: DC_Mot_Enc2.pin2, Part3.GND, Part3.PS1, HC-SR04_Sensor_1.GND, HC-SR04_Sensor_2.GND, HC-SR04_Sensor_3.GND, HC-SR04_Sensor_4.GND
  N19: DC_Mot_Enc2.pin5, Part3.3.3V, Part3.PS0
  VCC: HC-SR04_Sensor_1.VCC, HC-SR04_Sensor_2.VCC, HC-SR04_Sensor_3.VCC, HC-SR04_Sensor_4.VCC

custom parts:
  Raspberry Pi 5: The RPi5, a faster version of the awesome Raspberry Pi4B ARM Board with 40 pin gpio.
  L298N DC motor driver: 2x DC motor driver with 78M05 positive voltage regulator (7..35 V) L298N: max 46 V, 2 A Set 5 V Enable jumper to enable 5 V regultor (needed for the L298N) and +5 V output at screw terminal or supply external +5 V at screw terminal Set ENA and/or ENB to +5 V to enable motor permanently or supply ENA and/or ENB with PWM signal IN1 and IN2 set rotation directory for motor A (OUT1/OUT2) IN2 and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
